// Logisim project term_project.circ as structural Verilog: 10 circuits, main circuit main
module main (
);

  wire b0, b1, b2, b3, b4, b5, b6, b7, b8, b9, Check, Clear, correct, game_end, or_1_out, p_100, Play, Reset;
  wire [2:0] equal_display_1_col0, equal_display_1_col1, equal_display_1_col2, multi_display_1_col0,
       multi_display_1_col1, multi_display_1_col2;
  wire [3:0] a0, a1, m0, m1, p0, p1, q0, q1, s0, s1;

  Button button_1 (.out(Reset));
  Button button_2 (.out(Play));
  Hex_Digit_Display hex_digit_display_1 (.value(q0));  // open: dp
  Button button_3 (.out(Check));
  Button button_4 (.out(Clear));
  Hex_Digit_Display u_m1 (.value(m1));  // open: dp
  Hex_Digit_Display m2 (.value(m0));  // open: dp
  multi_display multi_display_1 (.col0(multi_display_1_col0), .col1(multi_display_1_col1), .col2(multi_display_1_col2));
  DotMatrix #(.matrixcols(3), .matrixrows(3)) dotmatrix_1 (
    .col0(multi_display_1_col2), .col1(multi_display_1_col1), .col2(multi_display_1_col0));
  Hex_Digit_Display hex_digit_display_2 (.value(q1));  // open: dp
  Button button_5 (.out(b0));
  Button button_6 (.out(b5));
  DotMatrix #(.matrixcols(1), .matrixrows(1)) dotmatrix_2 ();  // open: col0
  DotMatrix #(.matrixcols(1), .matrixrows(1)) dotmatrix_3 ();  // open: col0
  Hex_Digit_Display hex_digit_display_3 (.value(s1));  // open: dp
  Hex_Digit_Display points1 (.value(p1));  // open: dp
  Hex_Digit_Display points0 (.value(p0));  // open: dp
  equal_display equal_display_1 (.col0(equal_display_1_col0), .col1(equal_display_1_col1), .col2(equal_display_1_col2));
  DotMatrix #(.matrixcols(3), .matrixrows(3)) dotmatrix_4 (
    .col0(equal_display_1_col2), .col1(equal_display_1_col1), .col2(equal_display_1_col0));
  Button button_7 (.out(b1));
  Button button_8 (.out(b2));
  Button button_9 (.out(b6));
  Button button_10 (.out(b7));
  Hex_Digit_Display hex_digit_display_4 (.value(s0));  // open: dp
  Hex_Digit_Display hex_digit_display_5 (.value(a1));  // open: dp
  Hex_Digit_Display hex_digit_display_6 (.value(a0));  // open: dp
  Button button_11 (.out(b3));
  Button button_12 (.out(b4));
  Button button_13 (.out(b8));
  Button button_14 (.out(b9));
  calculator calculator_1 (.q0(q0), .q1(q1), .a0(a0), .a1(a1), .correct(correct));
  or or_1 (or_1_out, Play, Check);
  game_state game_state_1 (.start(Play), .reset(Reset), .p_100(p_100), .game_end(game_end));
  timer timer_1 (.set(Play), .reset(Reset), .game_end(game_end), .t0(s0), .t1(s1), .t2(m0), .t3(m1));
  random_number random_number_1 (.gen(or_1_out), .reset(Reset), .correct(correct), .R0(q0), .R1(q1));
  buttons buttons_1 (
    .reset(Reset), .check(Check), .clear(Clear), .game_end(game_end), .b0(b0), .b1(b1), .b2(b2), .b3(b3),
    .b4(b4), .b5(b5), .b6(b6), .b7(b7), .b8(b8), .b9(b9), .a1(a1), .a0(a0));
  points points_1 (
    .correct(correct), .reset(Reset), .game_end(game_end), .check(Check), .p0(p0), .p1(p1), .p_100(p_100));

  // Notes on the sheet:
  //   GOO GOO DAN 100
endmodule

module timer (
  input  set,
  input  reset,
  input  game_end,
  output [3:0] t0,
  output [3:0] t1,
  output [3:0] t2,
  output [3:0] t3
);

  wire a_hour, a_min, min10, or_1_out, or_2_out, or_3_out, sec10;

  Counter #(.max('h6), .width(4)) counter_1 (
    .clr(or_1_out), .clk(sec10), .carry(a_min), .Q(t1));  // open: load, up, count, D
  or or_1 (or_1_out, a_min, reset);
  Counter #(.max('h6), .width(4)) counter_2 (
    .clr(or_2_out), .clk(min10), .carry(a_hour), .Q(t3));  // open: load, up, count, D
  or or_2 (or_2_out, a_hour, reset);
  second_counter second_counter_1 (.set(set), .reset(reset), .game_end(game_end), .sec10(sec10), .s(t0));
  Counter #(.max('ha), .width(4)) counter_3 (
    .clr(or_3_out), .clk(a_min), .carry(min10), .Q(t2));  // open: load, up, count, D
  or or_3 (or_3_out, min10, reset);
endmodule

module second_counter (
  input  set,
  input  reset,
  input  game_end,
  output sec10,
  output [3:0] s
);

  wire a_sec, clk, not_1_out, or_1_out, or_2_out, s_r_ff_1_q, start;

  Clock clock_1 (.out(clk));
  or or_1 (or_1_out, a_sec, reset);
  Counter #(.max('h1b), .width(6)) counter_1 (
    .clr(or_1_out), .count(start), .clk(clk), .carry(a_sec));  // open: load, up, D, Q
  Counter #(.max('ha), .width(4)) counter_2 (
    .clr(or_2_out), .clk(a_sec), .carry(sec10), .Q(s));  // open: load, up, count, D
  or or_2 (or_2_out, sec10, reset);
  S_R_Flip_Flop s_r_ff_1 (.S(set), .R(reset), .clk(clk), .Q(s_r_ff_1_q));  // open: reset, Qn, preset
  not not_1 (not_1_out, game_end);
  and and_1 (start, s_r_ff_1_q, not_1_out);
endmodule

module random_number (
  input  gen,
  input  reset,
  input  correct,
  output [3:0] R0,
  output [3:0] R1
);

  wire and_1_out, clk0, clk1, counter_1_carry, counter_2_carry, get_edge;
  wire [3:0] adder_1_out, adder_2_out, R0_0to8, R1_0to8;

  Clock clock_1 (.out(clk0));
  Clock #(.highDuration(2)) clock_2 (.out(clk1));
  Counter #(.max('h9), .width(4)) counter_1 (
    .clr(counter_1_carry), .clk(clk0), .carry(counter_1_carry), .Q(R0_0to8));  // open: load, up, count, D
  Counter #(.max('h9), .width(4)) counter_2 (
    .clr(counter_2_carry), .clk(clk1), .carry(counter_2_carry), .Q(R1_0to8));  // open: load, up, count, D
  D_Flip_Flop d_ff_1 (.D(1'b1), .clk(and_1_out), .Q(get_edge), .reset(get_edge));  // open: Qn, preset
  and and_1 (and_1_out, gen, correct);
  Adder #(.width(4)) adder_1 (.a(R0_0to8), .b(4'b0001), .out(adder_1_out));  // open: cin, cout
  Adder #(.width(4)) adder_2 (.a(R1_0to8), .b(4'b0001), .out(adder_2_out));  // open: cin, cout
  D_Flip_Flop d_ff_2 (.D(adder_1_out[0]), .clk(get_edge), .Q(R0[0]), .reset(reset));  // open: Qn, preset
  D_Flip_Flop d_ff_3 (.D(adder_1_out[1]), .clk(get_edge), .Q(R0[1]), .reset(reset));  // open: Qn, preset
  D_Flip_Flop d_ff_4 (.D(adder_1_out[2]), .clk(get_edge), .Q(R0[2]), .reset(reset));  // open: Qn, preset
  D_Flip_Flop d_ff_5 (.D(adder_1_out[3]), .clk(get_edge), .Q(R0[3]), .reset(reset));  // open: Qn, preset
  D_Flip_Flop d_ff_6 (.D(adder_2_out[0]), .clk(get_edge), .Q(R1[0]), .reset(reset));  // open: Qn, preset
  D_Flip_Flop d_ff_7 (.D(adder_2_out[1]), .clk(get_edge), .Q(R1[1]), .reset(reset));  // open: Qn, preset
  D_Flip_Flop d_ff_8 (.D(adder_2_out[2]), .clk(get_edge), .Q(R1[2]), .reset(reset));  // open: Qn, preset
  D_Flip_Flop d_ff_9 (.D(adder_2_out[3]), .clk(get_edge), .Q(R1[3]), .reset(reset));  // open: Qn, preset

  // Other names for the same wires on the sheet: get = gen
endmodule

module buttons (
  input  reset,
  input  check,
  input  clear,
  input  game_end,
  input  b0,
  input  b1,
  input  b2,
  input  b3,
  input  b4,
  input  b5,
  input  b6,
  input  b7,
  input  b8,
  input  b9,
  output [3:0] a1,
  output [3:0] a0
);

  wire and_1_out, and_2_out, b_in, input_state, not_1_out, reset_t;
  wire [3:0] b_sel;

  or or_1 (reset_t, reset, check, clear);
  Priority_Encoder #(.select(4)) priority_encoder_1 (
    .in0(b0), .in1(b1), .in2(b2), .in3(b3), .in4(b4), .in5(b5), .in6(b6), .in7(b7), .in8(b8), .in9(b9),
    .out(b_sel), .gs(b_in));  // open: in10, in11, in12, in13, in14, in15, en_out, en_in
  D_Flip_Flop d_ff_1 (.D(1'b1), .clk(b_in), .Q(input_state), .reset(reset_t));  // open: Qn, preset
  and and_1 (and_1_out, b_in, ~game_end);  // AND_Gate
  Register #(.width(4)) a1reg (.D(b_sel), .en(not_1_out), .clk(and_1_out), .Q(a1), .clr(reset_t));
  not not_1 (not_1_out, input_state);
  Register #(.width(4)) a0reg (.D(b_sel), .en(input_state), .clk(and_2_out), .Q(a0), .clr(reset_t));
  and and_2 (and_2_out, b_in, ~game_end);  // AND_Gate
endmodule

module multi_display (
  output [2:0] col0,
  output [2:0] col1,
  output [2:0] col2
);


  assign col0 = 3'b101;
  assign col1 = 3'b010;
  assign col2 = 3'b101;
endmodule

module equal_display (
  output [2:0] col0,
  output [2:0] col1,
  output [2:0] col2
);


  assign col0 = 3'b101;
  assign col1 = 3'b101;
  assign col2 = 3'b101;
endmodule

module points (
  input  correct,
  input  reset,
  input  game_end,
  input  check,
  output [3:0] p0,
  output [3:0] p1,
  output p_100
);

  wire a_point, and_1_out, not_1_out, or_1_out, or_2_out, points_10;

  D_Flip_Flop d_ff_1 (.D(not_1_out), .clk(and_1_out), .Q(a_point), .reset(a_point));  // open: Qn, preset
  not not_1 (not_1_out, game_end);
  and and_1 (and_1_out, check, correct);
  Counter #(.max('ha), .width(4)) counter_1 (
    .clr(or_1_out), .clk(a_point), .carry(points_10), .Q(p0));  // open: load, up, count, D
  or or_1 (or_1_out, points_10, reset);
  Counter #(.max('ha), .width(4)) counter_2 (
    .clr(or_2_out), .clk(points_10), .carry(p_100), .Q(p1));  // open: load, up, count, D
  or or_2 (or_2_out, p_100, reset);

  // Other names for the same wires on the sheet: points_100 = p_100
endmodule

module calculator (
  input  [3:0] q0,
  input  [3:0] q1,
  input  [3:0] a0,
  input  [3:0] a1,
  output correct
);

  wire [7:0] ans_a, ans_q, bit_extender_1_out, bit_extender_2_out, bit_extender_3_out, bit_extender_4_out,
       multiplier_1_out;

  assign bit_extender_1_out = {{4{1'b0}}, q0};  // Bit_Extender bit_extender_1
  assign bit_extender_2_out = {{4{1'b0}}, q1};  // Bit_Extender bit_extender_2
  assign bit_extender_3_out = {{4{1'b0}}, a0};  // Bit_Extender bit_extender_3
  assign bit_extender_4_out = {{4{1'b0}}, a1};  // Bit_Extender bit_extender_4
  Multiplier multiplier_1 (.a(8'ha), .b(bit_extender_4_out), .out(multiplier_1_out));  // open: cin, cout
  Multiplier multiplier_2 (.a(bit_extender_1_out), .b(bit_extender_2_out), .out(ans_q));  // open: cin, cout
  Adder adder_1 (.a(bit_extender_3_out), .b(multiplier_1_out), .out(ans_a));  // open: cin, cout
  Comparator comparator_1 (.a(ans_q), .b(ans_a), .eq(correct));  // open: gt, lt
endmodule

module game_state (
  input  start,
  input  reset,
  input  p_100,
  output game_end
);

  wire and_1_out, clk, d_ff_1_q, or_1_out;

  Clock clock_1 (.out(clk));
  D_Flip_Flop d_ff_1 (.D(1'b1), .clk(and_1_out), .Q(d_ff_1_q), .reset(or_1_out));  // open: Qn, preset
  and and_1 (and_1_out, start, clk);
  or or_1 (or_1_out, reset, p_100);
  not not_1 (game_end, d_ff_1_q);
endmodule
